// Logisim project 1-bit-full-adder.circ as structural Verilog: 2 circuits, main circuit main
module main (
  input  Cin,
  input  A,
  input  B,
  output S,
  output Cout
);

  Adder #(.width(1)) adder_1 (.a(A), .b(B), .out(S), .cin(Cin), .cout(Cout));
endmodule

module _4_bit_ripple_carry (
  input  [3:0] A,
  input  [3:0] B,
  input  [3:0] A_2,
  input  [3:0] B_2,
  output [3:0] Sum,
  output Overflow,
  output [3:0] Sum_2,
  output Overflow_2
);

  wire main_1_cout, main_2_cout, main_3_cout, main_5_cout, main_6_cout, main_7_cout;

  main main_1 (.A(A[0]), .B(B[0]), .Cin(1'b0), .Cout(main_1_cout), .S(Sum[0]));
  main main_2 (.A(A[1]), .B(B[1]), .Cin(main_1_cout), .Cout(main_2_cout), .S(Sum[1]));
  main main_3 (.A(A[2]), .B(B[2]), .Cin(main_2_cout), .Cout(main_3_cout), .S(Sum[2]));
  main main_4 (.A(A[3]), .B(B[3]), .Cin(main_3_cout), .Cout(Overflow), .S(Sum[3]));
  main main_5 (.A(A_2[0]), .B(B_2[0]), .Cin(1'b0), .Cout(main_5_cout), .S(Sum_2[0]));
  main main_6 (.A(A_2[1]), .B(B_2[1]), .Cin(main_5_cout), .Cout(main_6_cout), .S(Sum_2[1]));
  main main_7 (.A(A_2[2]), .B(B_2[2]), .Cin(main_6_cout), .Cout(main_7_cout), .S(Sum_2[2]));
  main main_8 (.A(A_2[3]), .B(B_2[3]), .Cin(main_7_cout), .Cout(Overflow_2), .S(Sum_2[3]));
endmodule
