// Logisim project 1-bit-full-adder2.circ as structural Verilog: 2 circuits, main circuit main
module main (
  input  Cin,
  input  A,
  input  B,
  output S,
  output Cout
);

  Adder #(.width(1)) adder_1 (.a(A), .b(B), .out(S), .cin(Cin), .cout(Cout));
endmodule

module _4_bit_ripple_carry (
  input  [3:0] A,
  input  [3:0] B,
  output [3:0] Sum,
  output Overflow
);

  wire main_1_cout, main_2_cout, main_3_cout;

  main main_1 (.A(A[0]), .B(B[0]), .Cin(1'b0), .Cout(main_1_cout), .S(Sum[0]));
  main main_2 (.A(A[1]), .B(B[1]), .Cin(main_1_cout), .Cout(main_2_cout), .S(Sum[1]));
  main main_3 (.A(A[2]), .B(B[2]), .Cin(main_2_cout), .Cout(main_3_cout), .S(Sum[2]));
  main main_4 (.A(A[3]), .B(B[3]), .Cin(main_3_cout), .Cout(Overflow), .S(Sum[3]));
endmodule
