// Logisim project 412.circ as structural Verilog: 3 circuits, main circuit main
module main (
  input  D,
  input  R,
  input  S,
  output Q,
  output Q_prime,
  output Q_2,
  output Q_prime_2
);

  wire and_1_out, and_2_out, CLK_out, not_1_out;

  not not_1 (not_1_out, D);
  Clock CLK (.out(CLK_out));
  and and_1 (and_1_out, not_1_out, CLK_out);
  and and_2 (and_2_out, CLK_out, D);
  nor nor_1 (Q, and_1_out, Q_prime);
  nor nor_2 (Q_prime, Q, and_2_out);
  nor nor_3 (Q_2, R, Q_prime_2);
  nor nor_4 (Q_prime_2, Q_2, S);
endmodule

module _51 (
  input  Din,
  input  CLK,
  output Qout,
  output Q_prime_out
);

  wire main_1_q, not_1_out;

  main main_1 (.D(Din), .R(not_1_out), .Q(main_1_q));  // open: S, Q_prime, Q_2, Q_prime_2
  not not_1 (not_1_out, CLK);
  main main_2 (.D(main_1_q), .R(CLK), .Q(Qout), .Q_prime(Q_prime_out), .Q_2(Q_prime_out));  // open: S, Q_prime_2
endmodule

module _52 (
  input  in_1,
  input  [3:0] in_2,
  output [3:0] out_3
);

  _51 u_51_1 (.Din(in_2[0]), .CLK(in_1), .Qout(out_3[0]));  // open: Q_prime_out
  _51 u_51_2 (.Din(in_2[1]), .CLK(in_1), .Qout(out_3[1]));  // open: Q_prime_out
  _51 u_51_3 (.Din(in_2[2]), .CLK(in_1), .Qout(out_3[2]));  // open: Q_prime_out
  _51 u_51_4 (.Din(in_2[3]), .CLK(in_1), .Qout(out_3[3]));  // open: Q_prime_out
endmodule
