// Logisim project 6.circ as structural Verilog: 1 circuit, main circuit main
module main (
  input  [7:0] I,
  output [7:0] O
);

  wire button_1_out, clock_1_out;
  wire [7:0] multiplexer_1_out, not_1_out, register_1_q;

  Button button_1 (.out(button_1_out));
  assign not_1_out = ~I;  // NOT_Gate not_1, 8 bits wide
  Multiplexer #(.width(8), .enable("false")) multiplexer_1 (
    .in0(I), .in1(not_1_out), .out(multiplexer_1_out), .sel(button_1_out));
  Register register_1 (.D(O), .Q(register_1_q), .clk(clock_1_out));  // open: en, clr
  Clock clock_1 (.out(clock_1_out));
  Adder adder_1 (.a(register_1_q), .b(multiplexer_1_out), .out(O), .cin(button_1_out));  // open: cout
endmodule
