// Logisim project uppgf2.circ as structural Verilog: 1 circuit, main circuit main
module main (
  input  D0,
  input  D1,
  input  in_3,
  input  D2,
  input  D3,
  input  [1:0] S1_S0,
  output out_7
);

  wire multiplexer_1_out, multiplexer_2_out, multiplexer_3_out, multiplexer_4_out;

  Multiplexer #(.enable("false")) multiplexer_1 (.in0(D0), .in1(D1), .out(multiplexer_1_out), .sel(S1_S0[0]));
  Multiplexer #(.enable("false")) multiplexer_2 (.in0(D2), .in1(D3), .out(multiplexer_2_out), .sel(S1_S0[0]));
  Multiplexer #(.select(2)) multiplexer_3 (
    .in0(D0), .in1(D1), .in2(D2), .in3(D3), .out(multiplexer_3_out), .sel(S1_S0), .en(in_3));
  Multiplexer #(.enable("false")) multiplexer_4 (
    .in0(multiplexer_1_out), .in1(multiplexer_2_out), .out(multiplexer_4_out), .sel(S1_S0[1]));
  xor xor_1 (out_7, multiplexer_3_out, multiplexer_4_out);
endmodule
